# Fritzing sketch circuit (saved by Fritzing 0.9.3b)
breadboards: 1

parts:
  R1 = Resistor [tolerance=±5% resistance=220 package=THT]
  LED1 = LED - 5mm [color="Red (633nm)" package="5 mm [THT]"]
  Part1 = Arduino Uno (Rev3)
  Part2 = TRRS 3.5mm Jack Breakout
  R2 = Resistor [tolerance=±5% resistance=220 package=THT]
  LED2 = LED - 5mm [color="Blue (470nm)" package="5 mm [THT]"]
  R3 = Resistor [tolerance=±5% resistance=220 package=THT]
  LED3 = LED - 5mm [color="Green (555nm)" package="5 mm [THT]"]
  LED4 = LED - 5mm [color="Red (633nm)" package="5 mm [THT]"]
  R4 = Resistor [tolerance=±5% resistance=220 package=THT]

nets:
  N1: R1.Pin_0, LED1.cathode
  N2: R1.Pin_1, Part1.GND, R2.Pin_1, R3.Pin_1, R4.Pin_1
  N3: LED1.anode, Part1.D0/RX
  N4: Part1.A0, Part2.SLEEVE
  N5: Part1.A1, Part2.RING2
  N6: Part1.A2, Part2.RING1
  N7: Part1.A3, Part2.TIP
  N8: Part1.D1/TX, LED2.anode
  N9: Part1.D2, LED3.anode
  N10: Part1.D3_PWM, LED4.anode
  N11: R2.Pin_0, LED2.cathode
  N12: R3.Pin_0, LED3.cathode
  N13: LED4.cathode, R4.Pin_0
